# Fritzing sketch testing_setup (saved by Fritzing 0.9.3b)

parts:
  Part1 = Arduino Uno (Rev3)
  IC1 = IC, DIP package, 10 pins [chip_label=CC1101]

nets:
  N1: Part1.D11_PWM/MOSI, IC1.pin2
  N2: Part1.D12/MISO, IC1.pin3
  N3: Part1.D13/SCK, IC1.pin9
  N4: Part1.D2, IC1.pin7
  N5: Part1.3V3, IC1.pin1
  N6: Part1.GND, IC1.pin5
